# Fritzing sketch MidiGate (saved by Fritzing 0.9.3b)
breadboards: 1

parts:
  Part1 = Arduino Mega 2560 (Rev3)
  U1 = MIDI_CONN_FEMALE [package=din_5_female]
  U2 = LCD-16X2 [package=lcd-16x2_noholes]
  U3 = G3VM-61E1 [package=g3vm-61e1]
  U4 = MIDI_CONN_FEMALE [package=din_5_female]
  Part2 = SparkFun MIDI Shield
  U5 = MIDI_CONN_FEMALE [package=din_5_female]
  U6 = MIDI_CONN_FEMALE [package=din_5_female]
  R1 = Trimmer Potentiometer [maximum_resistance=10kΩ package=THT]
  R2 = Resistor [tolerance=±5% resistance=220 package="0603 [SMD]"]

nets:
  N1: Part1.D21/SCL, Part2.RX-I
  N2: Part1.D20/SDA, Part2.HARD-TX
  GND: Part1.GND, U2.VSS, U2.R_W, U2.K, U3.P$3, R1.leg1
  5V: Part1.5V, U2.VDD, U3.P$2, R1.leg2, R2.Pin_0
  N3: Part1.D31, U2.DB7
  N4: Part1.D33, U2.DB6
  N5: Part1.D35, U2.DB5
  N6: Part1.D37, U2.DB4
  N7: Part1.D39, U2.E
  N8: Part1.D41, U2.RS
  N9: Part1.D53, U3.P$1
  N10: U1.MIDI_IN, U3.P$4
  N11: U1.MIDI_OUT, U4.MIDI_OUT, U5.MIDI_OUT, U6.MIDI_OUT
  N12: U2.VO, R1.wiper
  N13: U2.A, R2.Pin_1
  N14: U3.P$5, U5.MIDI_IN
  N15: U3.P$6, U4.MIDI_IN, U6.MIDI_IN
